// Logisim project BALU.circ as structural Verilog: 1 circuit, main circuit main
module main (
  input  [31:0] in_1,
  input  [2:0] in_2,
  input  [31:0] in_3,
  output out_4
);

  wire comparator_1_eq, comparator_1_gt, comparator_1_lt, comparator_2_eq, comparator_2_gt, comparator_2_lt,
       not_1_out, or_1_out, or_2_out;

  Comparator #(.width(32)) comparator_1 (
    .a(in_1), .b(in_3), .gt(comparator_1_gt), .eq(comparator_1_eq), .lt(comparator_1_lt));
  Comparator #(.width(32), .mode("unsigned")) comparator_2 (
    .a(in_1), .b(in_3), .gt(comparator_2_gt), .eq(comparator_2_eq), .lt(comparator_2_lt));
  not not_1 (not_1_out, comparator_1_eq);
  or or_1 (or_1_out, comparator_2_gt, comparator_2_eq);
  or or_2 (or_2_out, comparator_1_gt, comparator_1_eq);
  Multiplexer #(.select(3)) multiplexer_1 (
    .in0(comparator_1_eq), .in1(not_1_out), .in3(comparator_1_lt), .in5(or_2_out), .in6(comparator_2_lt),
    .in7(or_1_out), .out(out_4), .sel(in_2));  // open: in2, in4, en

  // Notes on the sheet:
  //   BEQ
  //   BLT
  //   BGE
  //   BNE
endmodule
