// Logisim project CONTROLLER.circ as structural Verilog: 1 circuit, main circuit main
module main (
  input  [6:0] in_1,
  input  in_2,
  output out_3,
  output out_4,
  output out_5,
  output [1:0] out_6,
  output out_7,
  output out_8,
  output out_9,
  output [1:0] out_10,
  output [2:0] out_11,
  output [1:0] out_12
);

  wire main_1_auipc, main_1_b, main_1_i, main_1_j, main_1_jalr, main_1_lui, main_1_lw, main_1_r, main_1_s;

  decoder_cpu__main main_1 (
    .in_1(in_1), .r(main_1_r), .i(main_1_i), .s(main_1_s), .lui(main_1_lui), .b(main_1_b),
    .jalr(main_1_jalr), .lw(main_1_lw), .auipc(main_1_auipc), .j(main_1_j));
  control_decode_main main_2 (
    .R(main_1_r), .I(main_1_i), .Lui(main_1_lui), .Auipc(main_1_auipc), .Jal(main_1_j), .jalr(main_1_jalr),
    .lw(main_1_lw), .S(main_1_s), .B(main_1_b), .Reg_file(out_4), .Oper_B_sel(out_5), .Imm_Sel(out_6),
    .Mem_read(out_7), .Write_back(out_8), .Mem_write(out_9), .Next_Pc_sel(out_10), .Ope_A_Sel(out_12),
    .Alu_Op(out_11), .Jalr_2(out_3), .BNew(in_2));
endmodule
