// Logisim project Immediate (3).circ as structural Verilog: 1 circuit, main circuit main
module main (
  input  [31:0] in_1,
  input  [1:0] in_2,
  input  [31:0] in_3,
  output [31:0] out_4,
  output [31:0] B,
  output [31:0] J
);

  wire [11:0] bit_extender_1_out;
  wire [19:12] bit_extender_1_out_2;
  wire [31:0] shifter_1_out;

  assign {bit_extender_1_out_2, bit_extender_1_out} = {{19{1'b0}}, in_1[31]};  // Bit_Extender bit_extender_1
  Shifter #(.width(32)) shifter_1 (.in({bit_extender_1_out, in_1[31:12]}), .\dist (5'b01100), .out(shifter_1_out));
  Adder #(.width(32)) adder_1 (
    .a({bit_extender_1_out_2[18:12], bit_extender_1_out, in_1[31], in_1[7], in_1[30:25], in_1[11:8], 1'b0}),
    .b(in_3), .out(B), .cin(1'b0));  // open: cout
  Adder #(.width(32)) adder_2 (
    .a({bit_extender_1_out[10:0], in_1[31], in_1[19:12], in_1[20], in_1[30:21], 1'b0}), .b(in_3), .out(J),
    .cin(1'b0));  // open: cout
  Multiplexer #(.select(2), .width(32)) multiplexer_1 (
    .in0({bit_extender_1_out_2, bit_extender_1_out, in_1[31:20]}),
    .in1({bit_extender_1_out_2, bit_extender_1_out, in_1[31:25], in_1[11:7]}), .in2(shifter_1_out),
    .out(out_4), .sel(in_2));  // open: in3, en

  // Notes on the sheet:
  //   I
  //   S
  //   U
endmodule
