// Logisim project alu.circ as structural Verilog: 2 circuits, main circuit main
module main (
  input  in_1,
  input  [31:0] a,
  input  [3:0] in_3,
  input  [31:0] b,
  output cout,
  output [31:0] \output ,
  output out_7
);

  wire comparator_1_lt;
  wire [31:0] adder_1_out, and_1_out, multiplexer_2_out, or_1_out, shifter_1_out, subtractor_1_out, xor_1_out;

  Adder #(.width(32)) adder_1 (.a(a), .b(b), .out(adder_1_out), .cin(in_1), .cout(cout));
  Subtractor #(.width(32)) subtractor_1 (.a(a), .b(b), .out(subtractor_1_out), .bout(out_7));  // open: bin
  assign and_1_out = a & b;  // AND_Gate and_1, 32 bits wide
  assign or_1_out = a | b;  // OR_Gate or_1, 32 bits wide
  assign xor_1_out = a ^ b;  // XOR_Gate xor_1, 32 bits wide
  Shifter #(.width(32)) shifter_1 (.in(a), .\dist (b[4:0]), .out(shifter_1_out));
  Comparator #(.width(32)) comparator_1 (.a(a), .b(b), .lt(comparator_1_lt));  // open: gt, eq
  Multiplexer #(.select(4), .width(32)) multiplexer_1 (
    .in0(adder_1_out), .in1(subtractor_1_out), .in2(and_1_out), .in3(or_1_out), .in4(xor_1_out), .in5(b),
    .in6(shifter_1_out), .in7(multiplexer_2_out), .in14(b), .in15(b), .out(\output ), .sel(in_3));  // open: in8, in9, in10, in11, in12, in13, en
  Multiplexer #(.width(32)) multiplexer_2 (
    .in0({32{1'b0}}), .in1(32'h1), .out(multiplexer_2_out), .sel(comparator_1_lt));  // open: en

  // Notes on the sheet:
  //   arthematic unit
  //   logic unit
endmodule

module AU (
  input  [31:0] a,
  input  in_2,
  input  [31:0] b,
  output [31:0] \output 
);

  wire [31:0] adder_1_out, subtractor_1_out;

  Adder #(.width(32)) adder_1 (.a(a), .b(b), .out(adder_1_out));  // open: cin, cout
  Subtractor #(.width(32)) subtractor_1 (.a(a), .b(b), .out(subtractor_1_out));  // open: bin, bout
  Multiplexer #(.width(32), .enable("false")) multiplexer_1 (
    .in0(adder_1_out), .in1(subtractor_1_out), .out(\output ), .sel(in_2));
endmodule
