// Logisim project aluop.circ as structural Verilog
module TT_OP (
  input  R,
  input  I,
  input  S,
  input  AUIPC,
  input  LW,
  input  LUI,
  input  JAL,
  input  JALR,
  output OUT1,
  output OUT2,
  output OUT3
);

  wire and_1_out, and_2_out, and_3_out, and_4_out, and_5_out, and_6_out, not_1_out, not_2_out, not_3_out,
       not_4_out, not_5_out, not_6_out, not_7_out, not_8_out, not_9_out, not_10_out, not_11_out, not_12_out;

  not not_1 (not_1_out, R);
  and and_1 (and_1_out, not_1_out, not_2_out);
  not not_2 (not_2_out, I);
  not not_3 (not_3_out, LUI);
  and and_2 (and_2_out, not_3_out, not_4_out);
  not not_4 (not_4_out, JALR);
  not not_5 (not_5_out, R);
  and and_3 (and_3_out, not_5_out, not_6_out);
  not not_6 (not_6_out, S);
  not not_7 (not_7_out, AUIPC);
  and and_4 (and_4_out, not_7_out, not_8_out);
  not not_8 (not_8_out, LUI);
  not not_9 (not_9_out, R);
  and and_5 (and_5_out, not_9_out, not_10_out);
  not not_10 (not_10_out, I);
  not not_11 (not_11_out, S);
  and and_6 (and_6_out, not_11_out, not_12_out);
  not not_12 (not_12_out, LW);
  and and_7 (OUT1, and_1_out, and_2_out);
  and and_8 (OUT2, and_3_out, and_4_out);
  and and_9 (OUT3, and_5_out, and_6_out);
endmodule
