// Logisim project control decode.circ as structural Verilog: 1 circuit, main circuit main
module main (
  input  R,
  input  I,
  input  Lui,
  input  Auipc,
  input  Jal,
  input  jalr,
  input  lw,
  input  S,
  input  B,
  input  BNew,
  output Jalr_2,
  output Reg_file,
  output Oper_B_sel,
  output [1:0] Imm_Sel,
  output Mem_read,
  output Write_back,
  output Mem_write,
  output [1:0] Next_Pc_sel,
  output [2:0] Alu_Op,
  output [1:0] Ope_A_Sel
);

  wire and_1_out;

  and and_1 (and_1_out, B, BNew);
  or or_1 (Next_Pc_sel[0], jalr, and_1_out);
  or or_2 (Next_Pc_sel[1], Jal, jalr);
  or or_3 (Imm_Sel[0], R, S, and_1_out, Jal);
  or or_4 (Imm_Sel[1], R, and_1_out, Lui, Auipc, Jal);
  or or_5 (Reg_file, R, I, Lui, Auipc, Jal, jalr, lw);
  or or_6 (Oper_B_sel, I, Lui, Auipc, jalr, S, lw);
  or or_7 (Ope_A_Sel[0], Auipc, Lui);
  or or_8 (Ope_A_Sel[1], Lui, Jal);
  TT_OP tt_op_1 (
    .R(R), .I(I), .S(S), .AUIPC(lw), .LW(Auipc), .LUI(Lui), .JAL(Jal), .JALR(jalr), .OUT1(Alu_Op[2]),
    .OUT2(Alu_Op[1]), .OUT3(Alu_Op[0]));

  assign Jalr_2 = jalr;
  assign Mem_read = lw;
  assign Mem_write = S;
  assign Write_back = lw;
endmodule
