// Logisim project cpu.circ as structural Verilog: 1 circuit, main circuit main
module main (
  input  in_1,
  output out_2
);

  wire BALU_out_4, clock_1_out, main_2_out_4, main_2_out_5, main_2_out_7, main_2_out_8, main_2_out_9;
  wire [1:0] main_2_out_6, main_2_out_10, main_2_out_12;
  wire [2:0] main_2_out_11;
  wire [3:0] alucontrol_1_out_4;
  wire [31:0] adder_1_out, main_1_b, main_1_j, main_1_out_4, main_3_out_8, main_3_out_9, main_4_output,
       multiplexer_1_out, multiplexer_2_out, multiplexer_3_out, multiplexer_4_out, multiplexer_5_out,
       ram_1_data, register_q, rom_1_data;

  Multiplexer #(.select(2), .width(32)) multiplexer_1 (
    .in0(adder_1_out), .in1(main_1_b), .in2(main_1_j), .out(multiplexer_1_out), .sel(main_2_out_10));  // open: in3, en
  Clock clock_1 (.out(clock_1_out));
  Register #(.width(32)) register (.D(multiplexer_1_out), .Q(register_q), .clk(clock_1_out), .clr(in_1));  // open: en
  Adder #(.width(32)) adder_1 (.a(register_q), .b(32'h4), .out(adder_1_out));  // open: cin, cout
  ROM #(.addrWidth(10), .dataWidth(32)) rom_1 (.addr(register_q[11:2]), .data(rom_1_data));  // open: sel
  Immediate__3__main main_1 (
    .in_1(rom_1_data), .in_3(register_q), .out_4(main_1_out_4), .J(main_1_j), .in_2(main_2_out_6),
    .B(main_1_b));
  AluControl alucontrol_1 (
    .in_1(main_2_out_11), .in_2(register_q[14:12]), .FUNC7(register_q[30]), .out_4(alucontrol_1_out_4));
  CONTROLLER_main main_2 (
    .in_1(rom_1_data[6:0]), .in_2(BALU_out_4), .out_3(out_2), .out_4(main_2_out_4), .out_5(main_2_out_5),
    .out_6(main_2_out_6), .out_7(main_2_out_7), .out_8(main_2_out_8), .out_9(main_2_out_9),
    .out_10(main_2_out_10), .out_11(main_2_out_11), .out_12(main_2_out_12));
  register_file_main main_3 (
    .in_1(rom_1_data[19:15]), .in_2(rom_1_data[11:7]), .in_7(multiplexer_5_out), .in_4(rom_1_data[24:20]),
    .in_6(in_1), .out_8(main_3_out_8), .out_9(main_3_out_9), .in_5(clock_1_out), .in_3(main_2_out_4));
  Multiplexer #(.select(2), .width(32)) multiplexer_2 (
    .in0(main_3_out_8), .in1(adder_1_out), .in2(register_q), .out(multiplexer_2_out), .sel(main_2_out_12));  // open: in3, en
  Multiplexer #(.width(32)) multiplexer_3 (
    .in0(main_3_out_9), .in1(main_1_out_4), .out(multiplexer_3_out), .sel(main_2_out_5));  // open: en
  BALU_main BALU (.in_1(main_3_out_8), .in_2(register_q[14:12]), .in_3(main_3_out_9), .out_4(BALU_out_4));
  alu_main main_4 (
    .a(multiplexer_2_out), .b(multiplexer_3_out), .\output (main_4_output), .in_3(alucontrol_1_out_4));  // open: cout, out_7, in_1
  RAM #(.addrWidth(10), .dataWidth(32), .bus("separate")) ram_1 (
    .addr(main_4_output[11:2]), .din(main_3_out_9), .data(ram_1_data), .str(main_2_out_9), .ld(main_2_out_7));  // open: sel, clk, clr
  Multiplexer #(.width(32)) multiplexer_4 (
    .in0(main_4_output), .in1(ram_1_data), .out(multiplexer_4_out), .sel(main_2_out_8));  // open: en
  Multiplexer #(.width(32)) multiplexer_5 (
    .in0(multiplexer_4_out), .in1(adder_1_out), .out(multiplexer_5_out), .sel(out_2));  // open: en

  // Notes on the sheet:
  //   contents of rom_1 (hex, n*v repeats v):
  //   300193 400213 419463 4182b3 40320333
endmodule
