// Logisim project decoder(cpu).circ as structural Verilog: 1 circuit, main circuit main
module main (
  input  [6:0] in_1,
  output r,
  output i,
  output s,
  output lui,
  output b,
  output jalr,
  output lw,
  output auipc,
  output j
);

  Comparator #(.width(7)) comparator_1 (.a(in_1), .b(7'b0110011), .eq(r));  // open: gt, lt
  Comparator #(.width(7)) comparator_2 (.a(in_1), .b(7'b0010011), .eq(i));  // open: gt, lt
  Comparator #(.width(7)) comparator_3 (.a(in_1), .b(7'b0100011), .eq(s));  // open: gt, lt
  Comparator #(.width(7)) comparator_4 (.a(in_1), .b(7'b0110111), .eq(lui));  // open: gt, lt
  Comparator #(.width(7)) comparator_5 (.a(in_1), .b(7'b1100011), .eq(b));  // open: gt, lt
  Comparator #(.width(7)) comparator_6 (.a(in_1), .b(7'b1100111), .eq(jalr));  // open: gt, lt
  Comparator #(.width(7)) comparator_7 (.a(in_1), .b(7'b0000011), .eq(lw));  // open: gt, lt
  Comparator #(.width(7)) comparator_8 (.a(in_1), .b(7'b0010111), .eq(auipc));  // open: gt, lt
  Comparator #(.width(7)) comparator_9 (.a(in_1), .b(7'b1101111), .eq(j));  // open: gt, lt
endmodule
